# Fritzing sketch F1Wheel (saved by Fritzing 0.9.5d)

parts:
  Pro_Micro1 = SparkFun Pro Micro
  B_8 = Round Pushbutton  # not connected
  B_7 = Round Pushbutton  # not connected
  B_9 = Round Pushbutton  # not connected
  B_11 = Round Pushbutton  # not connected
  B_10 = Round Pushbutton  # not connected
  B_12 = Round Pushbutton  # not connected
  B_16 = Round Pushbutton
  B_15 = Round Pushbutton
  B_18 = Round Pushbutton
  B_14 = Round Pushbutton
  B_13 = Round Pushbutton
  B_17 = Round Pushbutton
  B_1 = Square Pushbutton
  B_31 = Square Pushbutton
  B_2 = Square Pushbutton
  B_32 = Square Pushbutton

nets:
  N1: Pro_Micro1.GND, B_1.leg0
  N2: Pro_Micro1.5, B_31.leg1
  N3: Pro_Micro1.6, B_32.leg1
  N4: Pro_Micro1.7, B_2.leg1
  N5: B_16.leg1, B_14.leg0
  N6: B_15.leg1, B_13.leg0
  N7: B_18.leg1, B_17.leg0

custom parts:
  SparkFun Pro Micro: The Pro Micro is similar to the Pro Mini except with an ATmega32U4 on board. The USB transceiver inside the 32U4 allows us to add USB connectivity on-board and do away with bulky external USB interface. Based on: https://github.com/unorthodox-engineers/unorthodox-arduino/blob/master/Unorthodox/fritzing/parts/Pro%20Micro.fzpz
